// Logisim project log.circ as structural Verilog: 7 circuits, main circuit motherboard
module motherboard (
);

  wire clock_1_out;
  wire [1:0] n8080_1_p3;
  wire [7:0] n8080_1_p2;
  wire [15:0] n8080_1_p1;

  Clock clock_1 (.out(clock_1_out));
  // _8080 8080_1: pin names not known; wires that end beside it: n8080_1_p1, n8080_1_p2, n8080_1_p3
  // Probe on n8080_1_p1
  // Probe on n8080_1_p2
  RAM #(.addrWidth(16)) ram_1 (
    .addr(n8080_1_p1), .data(n8080_1_p2), .clk(n8080_1_p3[1]), .ld(n8080_1_p3[0]));  // open: sel, clr
  TTY tty_1 ();  // open: data, clk, we, clr
endmodule

module FLG (
  input  [3:0] in_1,
  input  [1:0] in_2,
  output t_f
);

  wire [3:0] and_1_out, decoder_1_out0;

  Decoder #(.select(2), .disabled(0), .enable("false")) decoder_1 (
    .out0(decoder_1_out0[0]), .out1(decoder_1_out0[1]), .out2(decoder_1_out0[2]), .out3(decoder_1_out0[3]),
    .sel(in_2));
  Pull_Resistor pull_resistor_1 (.node(in_1));
  Pull_Resistor pull_resistor_2 (.node(decoder_1_out0));
  // Probe on and_1_out
  assign and_1_out = in_1 & decoder_1_out0;  // AND_Gate and_1, 4 bits wide
  or or_1 (t_f, and_1_out[0], and_1_out[1], and_1_out[2], and_1_out[3]);
endmodule

module ALU (
  input  [2:0] in_1,
  input  [7:0] A,
  input  [7:0] B,
  input  [3:0] in_4,
  input  en,
  output [7:0] out_6,
  output [3:0] out_7
);

  wire adder_1_cout, and_2_out, and_3_out, not_2_out, not_3_out, not_4_out, not_5_out, not_6_out,
       subtractor_1_bout;
  wire [3:0] bitadder_1_out;
  wire [7:0] adder_1_out, and_1_out, not_1_out, or_1_out, subtractor_1_out, undriven, undriven_2, xor_1_out;

  Pull_Resistor pull_resistor_1 (.node(A));
  assign not_1_out = ~A;  // NOT_Gate not_1, 8 bits wide
  Adder adder_1 (.a(A), .b(B), .out(adder_1_out), .cin(in_4[0]), .cout(adder_1_cout));
  assign out_7[0] = and_3_out ? adder_1_cout : 1'bz;  // Controlled_Buffer controlled_buffer_1
  Subtractor subtractor_1 (.a(A), .b(B), .out(subtractor_1_out), .bin(in_4[0]), .bout(subtractor_1_bout));
  assign out_7[0] = and_2_out ? subtractor_1_bout : 1'bz;  // Controlled_Buffer controlled_buffer_2
  assign and_1_out = A & B;  // AND_Gate and_1, 8 bits wide
  assign or_1_out = A | B;  // OR_Gate or_1, 8 bits wide
  assign xor_1_out = A ^ B;  // XOR_Gate xor_1, 8 bits wide
  Comparator comparator_1 (.a(A), .b(B), .gt(out_7[1]), .eq(out_7[2]));  // open: lt
  BitAdder bitadder_1 (.in0(A), .out(bitadder_1_out));
  nor nor_1 (out_7[3], bitadder_1_out[0], bitadder_1_out[1], bitadder_1_out[2], bitadder_1_out[3]);
  not not_2 (not_2_out, in_1[1]);
  and and_2 (and_2_out, in_1[0], not_2_out, not_3_out);
  not not_3 (not_3_out, in_1[2]);
  not not_4 (not_4_out, in_1[0]);
  and and_3 (and_3_out, not_4_out, not_5_out, not_6_out);
  not not_5 (not_5_out, in_1[1]);
  not not_6 (not_6_out, in_1[2]);
  Multiplexer #(.select(3), .width(8)) multiplexer_1 (
    .in0(adder_1_out), .in1(subtractor_1_out), .in2(and_1_out), .in3(or_1_out), .in4(xor_1_out),
    .in5(not_1_out), .in6(undriven), .in7(undriven_2), .out(out_6), .sel(in_1), .en(en));
endmodule

module Timer (
  input  sRST,
  input  clk,
  output [3:0] ct,
  output e,
  output s
);

  wire and_1_out, decoder_1_out0, decoder_1_out1, decoder_1_out2, not_1_out, t_ff_1_q;
  wire [1:0] t_ff_2_q;

  not not_1 (not_1_out, clk);
  T_Flip_Flop t_ff_1 (.clk(sRST), .T(sRST), .Q(t_ff_1_q), .reset(decoder_1_out0));  // open: Qn, preset, en
  T_Flip_Flop t_ff_2 (.clk(not_1_out), .T(not_1_out), .Q(t_ff_2_q[0]));  // open: Qn, preset, reset, en
  T_Flip_Flop t_ff_3 (.clk(clk), .T(clk), .Q(t_ff_2_q[1]));  // open: Qn, preset, reset, en
  and and_1 (and_1_out, t_ff_1_q, decoder_1_out0);
  Decoder #(.select(2), .disabled(0), .enable("false")) decoder_1 (
    .out0(decoder_1_out0), .out1(decoder_1_out1), .out2(decoder_1_out2), .out3(s), .sel(t_ff_2_q));
  Counter #(.width(4), .max('hf)) counter_1 (
    .Q(ct), .clk(decoder_1_out0), .clr(and_1_out));  // open: load, D, count, carry
  or or_1 (e, decoder_1_out1, decoder_1_out2, s);
endmodule

module _8080 (
  output [7:0] out_1
);

  wire clock_1_out, control_unit_1_ealu, control_unit_1_sbus, control_unit_1_sin, control_unit_1_srst,
       control_unit_1_stmp, timer_1_e, timer_1_s;
  wire [1:0] control_unit_1_e_s_acc, control_unit_1_e_s_flg, control_unit_1_e_s_ra, control_unit_1_e_s_ram,
       control_unit_1_e_s_sp;
  wire [2:0] control_unit_1_op, control_unit_1_reg;
  wire [3:0] alu_1_out_7, control_unit_1_e_s_ct_ld_adb, control_unit_1_e_s_ct_ld_pc,
       control_unit_1_hl_e_s_hl, controlled_buffer_2_out, register_3_q, timer_1_ct;
  wire [7:0] controlled_buffer_1_out, register_1_q, register_2_q, register_4_q;
  wire [15:0] regfile_1_out_9;

  assign controlled_buffer_1_out = control_unit_1_e_s_acc[1] ? register_1_q : 8'bz;  // Controlled_Buffer controlled_buffer_1
  Register #(.trigger("falling")) register_1 (
    .D(controlled_buffer_1_out), .Q(register_1_q), .clk(control_unit_1_e_s_acc[0]));  // open: en, clr
  Register register_2 (.D(controlled_buffer_1_out), .Q(register_2_q), .clk(control_unit_1_stmp));  // open: en, clr
  Register #(.width(4)) register_3 (
    .D(alu_1_out_7), .Q(register_3_q), .clk(control_unit_1_e_s_flg[1]));  // open: en, clr
  assign controlled_buffer_2_out = control_unit_1_e_s_flg[0] ? register_3_q : 4'bz;  // Controlled_Buffer controlled_buffer_2
  ALU alu_1 (
    .in_4(controlled_buffer_2_out), .A(register_1_q), .B(register_2_q), .in_1(control_unit_1_op),
    .out_6(controlled_buffer_1_out), .out_7(alu_1_out_7), .en(control_unit_1_ealu));
  control_unit control_unit_1 (
    .e(timer_1_e), .s(timer_1_s), .ct(timer_1_ct), .e_s_ACC(control_unit_1_e_s_acc),
    .sTMP(control_unit_1_stmp), .eALU(control_unit_1_ealu), .e_s_FLG(control_unit_1_e_s_flg),
    .OP(control_unit_1_op), .sRST(control_unit_1_srst), .e_s_ct_LD_ADB(control_unit_1_e_s_ct_ld_adb),
    .e_s_ct_ld_PC(control_unit_1_e_s_ct_ld_pc), .e_s_SP(control_unit_1_e_s_sp),
    .hl_e_s_HL(control_unit_1_hl_e_s_hl), .e_s_RA(control_unit_1_e_s_ra), .e_s_RAM(control_unit_1_e_s_ram),
    .sIN(control_unit_1_sin), .INST(register_4_q), .REG(control_unit_1_reg),
    .flg_in(controlled_buffer_2_out), .sBUS(control_unit_1_sbus));
  Timer timer_1 (.sRST(control_unit_1_srst), .ct(timer_1_ct), .e(timer_1_e), .s(timer_1_s), .clk(clock_1_out));
  Clock clock_1 (.out(clock_1_out));
  Register register_4 (.D(controlled_buffer_1_out), .Q(register_4_q), .clk(control_unit_1_sin));  // open: en, clr
  Register register_5 (.D(controlled_buffer_1_out), .Q(out_1), .clk(control_unit_1_sbus));  // open: en, clr
  regfile regfile_1 (
    .in_1(controlled_buffer_1_out), .out_8(controlled_buffer_1_out), .in_3(control_unit_1_e_s_ra),
    .in_5(control_unit_1_reg), .adb(control_unit_1_e_s_ct_ld_adb), .pc(control_unit_1_e_s_ct_ld_pc),
    .sp(control_unit_1_e_s_sp), .out_9(regfile_1_out_9), .in_2(control_unit_1_hl_e_s_hl));
  RAM #(.addrWidth(16)) ram_1 (
    .addr(regfile_1_out_9), .data(controlled_buffer_1_out), .clk(control_unit_1_e_s_ram[1]),
    .ld(control_unit_1_e_s_ram[0]));  // open: sel, clr
endmodule

module regfile (
  input  [7:0] in_1,
  input  [3:0] in_2,
  input  [1:0] in_3,
  input  [3:0] adb,
  input  [2:0] in_5,
  input  [3:0] pc,
  input  [1:0] sp,
  output [7:0] out_8,
  output [15:0] out_9
);

  wire or_1_out;
  wire [1:0] demultiplexer_1_out0, demultiplexer_1_out1, demultiplexer_1_out2, demultiplexer_1_out3;
  wire [7:0] buffer_2_out, controlled_buffer_1_out, controlled_buffer_2_out, controlled_buffer_6_out,
       demultiplexer_2_out0, demultiplexer_2_out1, register_1_q, register_2_q, register_3_q, register_4_q,
       register_5_q, register_6_q, register_7_q, register_8_q, register_9_q, register_10_q;
  wire [15:0] counter_1_q, counter_2_q, register_11_q;

  or or_1 (or_1_out, in_2[2], in_5[2]);
  Demultiplexer #(.select(2), .width(2), .disabled(0), .enable("false")) demultiplexer_1 (
    .out0(demultiplexer_1_out0), .out1(demultiplexer_1_out1), .out2(demultiplexer_1_out2),
    .out3(demultiplexer_1_out3), .in(in_3), .sel(in_5[1:0]));
  Demultiplexer #(.width(8), .tristate("true"), .disabled(0), .enable("false")) demultiplexer_2 (
    .out0(demultiplexer_2_out0), .out1(demultiplexer_2_out1), .in(in_1), .sel(or_1_out));
  assign demultiplexer_2_out1 = controlled_buffer_1_out;  // Buffer buffer_1, 8 bits wide
  assign controlled_buffer_1_out = in_2[1] ? register_1_q : 8'bz;  // Controlled_Buffer controlled_buffer_1
  Register register_1 (.D(demultiplexer_2_out0), .Q(register_1_q), .clk(in_2[0]));  // open: en, clr
  Register register_2 (.D(demultiplexer_2_out0), .Q(register_2_q), .clk(demultiplexer_1_out0[0]));  // open: en, clr
  assign controlled_buffer_2_out = demultiplexer_1_out0[1] ? register_2_q : 8'bz;  // Controlled_Buffer controlled_buffer_2
  assign controlled_buffer_2_out = demultiplexer_1_out1[1] ? register_3_q : 8'bz;  // Controlled_Buffer controlled_buffer_3
  Register register_3 (.D(demultiplexer_2_out0), .Q(register_3_q), .clk(demultiplexer_1_out1[0]));  // open: en, clr
  Register register_4 (.D(demultiplexer_2_out0), .Q(register_4_q), .clk(demultiplexer_1_out2[0]));  // open: en, clr
  assign controlled_buffer_2_out = demultiplexer_1_out2[1] ? register_4_q : 8'bz;  // Controlled_Buffer controlled_buffer_4
  Register register_5 (.D(demultiplexer_2_out0), .Q(register_5_q), .clk(demultiplexer_1_out3[0]));  // open: en, clr
  assign controlled_buffer_2_out = demultiplexer_1_out3[1] ? register_5_q : 8'bz;  // Controlled_Buffer controlled_buffer_5
  Multiplexer #(.width(8), .disabled(0), .enable("false")) multiplexer_1 (
    .in0(controlled_buffer_2_out), .in1(buffer_2_out), .out(out_8), .sel(or_1_out));
  assign buffer_2_out = controlled_buffer_6_out;  // Buffer buffer_2, 8 bits wide
  Register register_6 (.D(demultiplexer_2_out1), .Q(register_6_q), .clk(in_2[0]));  // open: en, clr
  assign controlled_buffer_6_out = in_2[1] ? register_6_q : 8'bz;  // Controlled_Buffer controlled_buffer_6
  assign buffer_2_out = demultiplexer_1_out0[1] ? register_7_q : 8'bz;  // Controlled_Buffer controlled_buffer_7
  Register register_7 (.D(demultiplexer_2_out1), .Q(register_7_q), .clk(demultiplexer_1_out0[0]));  // open: en, clr
  assign buffer_2_out = demultiplexer_1_out1[1] ? register_8_q : 8'bz;  // Controlled_Buffer controlled_buffer_8
  Register register_8 (.D(demultiplexer_2_out1), .Q(register_8_q), .clk(demultiplexer_1_out1[0]));  // open: en, clr
  Register register_9 (.D(demultiplexer_2_out1), .Q(register_9_q), .clk(demultiplexer_1_out2[0]));  // open: en, clr
  assign buffer_2_out = demultiplexer_1_out2[1] ? register_9_q : 8'bz;  // Controlled_Buffer controlled_buffer_9
  assign buffer_2_out = demultiplexer_1_out3[1] ? register_10_q : 8'bz;  // Controlled_Buffer controlled_buffer_10
  Register register_10 (.D(demultiplexer_2_out1), .Q(register_10_q), .clk(demultiplexer_1_out3[0]));  // open: en, clr
  assign out_9 = in_2[3] ? {controlled_buffer_1_out, controlled_buffer_6_out} : 16'bz;  // Controlled_Buffer controlled_buffer_11
  Counter #(.width(16), .max('hffff)) counter_1 (
    .load(adb[0]), .D({buffer_2_out, controlled_buffer_2_out}), .count(adb[1]), .Q(counter_1_q), .clk(adb[2]));  // open: carry, clr
  assign out_9 = adb[3] ? counter_1_q : 16'bz;  // Controlled_Buffer controlled_buffer_12
  assign out_9 = pc[3] ? counter_2_q : 16'bz;  // Controlled_Buffer controlled_buffer_13
  Counter #(.width(16), .max('hffff)) counter_2 (
    .load(pc[0]), .D({buffer_2_out, controlled_buffer_2_out}), .count(pc[1]), .Q(counter_2_q), .clk(pc[2]));  // open: carry, clr
  Register #(.width(16)) register_11 (
    .D({buffer_2_out, controlled_buffer_2_out}), .Q(register_11_q), .clk(sp[0]));  // open: en, clr
  assign out_9 = sp[1] ? register_11_q : 16'bz;  // Controlled_Buffer controlled_buffer_14
  assign {demultiplexer_2_out1, demultiplexer_2_out0} = out_9;  // Buffer buffer_3, 16 bits wide
endmodule

module control_unit (
  input  s,
  input  [7:0] INST,
  input  [3:0] flg_in,
  input  [3:0] ct,
  input  e,
  output sBUS,
  output sIN,
  output [1:0] e_s_RAM,
  output [1:0] e_s_ACC,
  output sTMP,
  output eALU,
  output [1:0] e_s_FLG,
  output [2:0] OP,
  output sRST,
  output [3:0] e_s_ct_LD_ADB,
  output [3:0] e_s_ct_ld_PC,
  output [1:0] e_s_SP,
  output [3:0] hl_e_s_HL,
  output [2:0] REG,
  output [1:0] e_s_RA
);

  wire [9:9] flg_1_t_f;
  wire [19:18] controlled_buffer_2_out;
  wire [31:0] rom_1_data;

  FLG flg_1 (.in_1(flg_in), .t_f(flg_1_t_f[9]), .in_2(INST[1:0]));
  assign {sBUS, sIN, e_s_RAM[0], e_s_ACC[0], sTMP, e_s_FLG[0], sRST, e_s_ct_LD_ADB[2], e_s_ct_ld_PC[2], e_s_SP[0], hl_e_s_HL[0], e_s_RA[0]} = s ? rom_1_data[11:0] : 12'bz;  // Controlled_Buffer controlled_buffer_1
  ROM #(.addrWidth(10), .dataWidth(32)) rom_1 (.addr({flg_1_t_f[9], INST[7:3], ct}), .data(rom_1_data));  // open: sel
  assign {controlled_buffer_2_out, hl_e_s_HL[3], e_s_RAM[1], e_s_ACC[1], eALU, e_s_FLG[1], OP[0], OP[1], OP[2], e_s_ct_LD_ADB[0], e_s_ct_LD_ADB[1], e_s_ct_LD_ADB[3], e_s_ct_ld_PC[0], e_s_ct_ld_PC[1], e_s_ct_ld_PC[3], e_s_SP[1], hl_e_s_HL[2:1], e_s_RA[1]} = e ? rom_1_data[31:12] : 20'bz;  // Controlled_Buffer controlled_buffer_2
  Pull_Resistor pull_resistor_1 (.node({sBUS, sIN, e_s_RAM[0], e_s_ACC[0], sTMP, e_s_FLG[0], sRST, e_s_ct_LD_ADB[2], e_s_ct_ld_PC[2], e_s_SP[0], hl_e_s_HL[0], e_s_RA[0]}));
  Pull_Resistor pull_resistor_2 (.node({controlled_buffer_2_out, hl_e_s_HL[3], e_s_RAM[1], e_s_ACC[1], eALU, e_s_FLG[1], OP[0], OP[1], OP[2], e_s_ct_LD_ADB[0], e_s_ct_LD_ADB[1], e_s_ct_LD_ADB[3], e_s_ct_ld_PC[0], e_s_ct_ld_PC[1], e_s_ct_ld_PC[3], e_s_SP[1], hl_e_s_HL[2:1], e_s_RA[1]}));

  assign REG = INST[2:0];

  // Notes on the sheet:
  //   contents of rom_1 (hex, n*v repeats v):
  //   0 4352 32 13*0 68633096 34217729 32 13*0 68633096 68632073 32
endmodule
