// Logisim project logv2.circ as structural Verilog: 8 circuits, main circuit motherboard
module motherboard (
);

  wire clock_1_out;
  wire [1:0] undriven_2;
  wire [7:0] ram_1_data;
  wire [15:0] undriven;

  CPU cpu_1 (.ClkIn(clock_1_out));  // open: in_2, in_1
  Clock clock_1 (.out(clock_1_out));
  // Probe on undriven
  // Probe on ram_1_data
  RAM #(.addrWidth(16)) ram_1 (
    .addr(undriven), .data(ram_1_data), .clk(undriven_2[1]), .ld(undriven_2[0]));  // open: sel, clr
  TTY tty_1 ();  // open: data, clk, we, clr
endmodule

module CPU (
  input  [4:0] in_1,
  input  [7:0] in_2,
  input  ClkIn
);

  wire and_1_out, clock_1_out, decoder_1_out0, decoder_1_out1, decoder_1_out2, decoder_1_out3, not_1_out,
       or_1_out, t_ff_1_q, undriven_6, undriven_8, undriven_11;
  wire [1:0] t_ff_3_q, undriven_2, undriven_3, undriven_4, undriven_5, undriven_7, undriven_9, undriven_10;
  wire [2:0] undriven_12, undriven_13;
  wire [3:0] counter_1_q, register_1_q, undriven;
  wire [7:0] n16_2_reg_1__8_out, n16_2_reg_1_probe_gsb, n16_2_reg_1_probe_lsb, n16_2_reg_2_probe_gsb,
       n16_2_reg_2_probe_lsb;
  wire [10:10] flg_1_t_f;
  wire [15:0] alu_1_out, controlled_buffer_2_out, controlled_buffer_3_out, counter_2_q, n16_1_reg_1__16_out,
       n16_2_reg_1__16_out, register_2_q, register_3_q, register_4_q, register_5_q, shreg_1_out_3,
       shreg_2_out_3;
  wire [31:0] rom_1_data;

  shreg shreg_1 (.in_1(n16_2_reg_1__8_out), .in_2(controlled_buffer_2_out[9]), .out_3(shreg_1_out_3));
  not not_1 (not_1_out, clock_1_out);
  Clock clock_1 (.out(clock_1_out));
  Register #(.width(4)) register_1 (.D(undriven), .Q(register_1_q), .clk(controlled_buffer_2_out[8]));  // open: en, clr
  Register #(.width(16)) register_2 (
    .D(shreg_1_out_3), .Q(register_2_q), .clk(controlled_buffer_2_out[11]));  // open: en, clr
  // Probe on register_2_q[15:10]
  and and_1 (and_1_out, t_ff_1_q, decoder_1_out0);
  T_Flip_Flop t_ff_1 (
    .clk(controlled_buffer_2_out[10]), .T(controlled_buffer_2_out[10]), .Q(t_ff_1_q), .reset(decoder_1_out1));  // open: Qn, preset, en
  T_Flip_Flop t_ff_2 (.clk(not_1_out), .T(not_1_out), .Q(t_ff_3_q[1]));  // open: Qn, preset, reset, en
  T_Flip_Flop t_ff_3 (.clk(clock_1_out), .T(clock_1_out), .Q(t_ff_3_q[0]));  // open: Qn, preset, reset, en
  _16_2_reg u_16_2_reg_1 (
    ._8_in(n16_2_reg_1__8_out), ._16_in(n16_2_reg_1__16_out), ._16_out(n16_2_reg_1__16_out),
    ._8_out(n16_2_reg_1__8_out), ._16_LH(undriven_2), .E_S(undriven_3), .probe_LSB(n16_2_reg_1_probe_lsb),
    .probe_GSB(n16_2_reg_1_probe_gsb));
  // Probe on n16_2_reg_1_probe_gsb
  // Probe on n16_2_reg_1_probe_lsb
  FLG flg_1 (.in_1(register_1_q), .cgez(register_2_q[9:6]), .t_f(flg_1_t_f[10]));
  Counter #(.width(4), .max('hf)) counter_1 (
    .Q(counter_1_q), .clk(decoder_1_out0), .clr(and_1_out));  // open: load, D, count, carry
  Decoder #(.select(2), .disabled(0), .enable("false")) decoder_1 (
    .out0(decoder_1_out0), .out1(decoder_1_out1), .out2(decoder_1_out2), .out3(decoder_1_out3), .sel(t_ff_3_q));
  _16_2_reg u_16_2_reg_2 (
    ._8_in(n16_2_reg_1__8_out), ._16_in(n16_2_reg_1__16_out), ._16_out(n16_2_reg_1__16_out),
    ._8_out(n16_2_reg_1__8_out), ._16_LH(undriven_4), .E_S(undriven_5), .probe_LSB(n16_2_reg_2_probe_lsb),
    .probe_GSB(n16_2_reg_2_probe_gsb));
  // Probe on n16_2_reg_2_probe_gsb
  // Probe on n16_2_reg_2_probe_lsb
  or or_1 (or_1_out, decoder_1_out1, decoder_1_out2, decoder_1_out3);
  Register #(.width(16)) register_3 (
    .D(n16_2_reg_1__16_out), .Q(register_3_q), .clk(undriven_7[1]), .clr(undriven_6));  // open: en
  ROM #(.addrWidth(11), .dataWidth(32)) rom_1 (
    .addr({flg_1_t_f[10], register_2_q[15:10], counter_1_q}), .data(rom_1_data));  // open: sel
  Register #(.width(16)) register_4 (
    .D(n16_2_reg_1__16_out), .Q(register_4_q), .clk(undriven_9[1]), .clr(undriven_8));  // open: en
  assign n16_2_reg_1__16_out = undriven_7[0] ? register_3_q : 16'bz;  // Controlled_Buffer controlled_buffer_1
  // Probe on register_2_q[5:0]
  assign controlled_buffer_2_out = decoder_1_out3 ? rom_1_data[15:0] : 16'bz;  // Controlled_Buffer controlled_buffer_2
  Pull_Resistor pull_resistor_1 (.node(controlled_buffer_2_out));
  assign controlled_buffer_3_out = or_1_out ? rom_1_data[31:16] : 16'bz;  // Controlled_Buffer controlled_buffer_3
  Pull_Resistor pull_resistor_2 (.node(controlled_buffer_3_out));
  // Probe on in_2
  shreg shreg_2 (.in_1(n16_2_reg_1__8_out), .in_2(in_1[4]), .out_3(shreg_2_out_3));
  assign n16_2_reg_1__16_out = undriven_9[0] ? register_4_q : 16'bz;  // Controlled_Buffer controlled_buffer_4
  Counter #(.width(16), .max('hffff)) counter_2 (
    .load(in_1[3]), .D(shreg_2_out_3), .count(in_1[2]), .Q(counter_2_q), .clk(in_1[1]));  // open: carry, clr
  assign n16_2_reg_1__16_out = in_1[0] ? counter_2_q : 16'bz;  // Controlled_Buffer controlled_buffer_5
  Register #(.width(16)) register_5 (.D(n16_2_reg_1__16_out), .Q(register_5_q), .clk(undriven_11));  // open: en, clr
  ALU alu_1 (
    .A(n16_2_reg_1__16_out), .B(n16_1_reg_1__16_out), .out(alu_1_out), .A_8(n16_2_reg_1__8_out));  // open: Carry_in, C_G_E_Z, _16, OP
  _16_1_reg u_16_1_reg_1 (
    ._16_S_E(undriven_13), ._16_in(n16_2_reg_1__16_out), ._8_in(n16_2_reg_1__8_out),
    ._16_out(n16_1_reg_1__16_out));  // open: _8_out
  _16_1_reg u_16_1_reg_2 (
    ._16_S_E(undriven_12), ._16_in(alu_1_out), ._8_out(n16_2_reg_1__8_out), ._16_out(n16_2_reg_1__16_out));  // open: _8_in
  RAM #(.addrWidth(16)) ram_1 (
    .addr(register_5_q), .data(n16_2_reg_1__8_out), .clk(undriven_10[1]), .ld(undriven_10[0]));  // open: sel, clr

  // Notes on the sheet:
  //   contents of rom_1 (hex, n*v repeats v):
  //   80004 500208 80004 500208 800 400 10*0 80004 500208 80004 500208 800 80004 501008 400 8*0 80004
  //   500208 80004 500208 800 80004 d0000a 1800001 810004 4000080 400 5*0 80004 500208 80004 500208 800
  //   80004 d0000a 1800001 810004 401000 400 5*0 80004 500208 80004 500208 800 8000002 4000001 12000 400
  //   7*0 80004 500208 80004 500208 800 8000002 4020001 12000 400 7*0 80004 500208 80004 500208 800
  //   8000002 4040001 12000 400 7*0 80004 500208 80004 500208 800 8000002 4060100 400 8*0 80004 500208
  //   80004 500208 800 80004 500018 80004 500018 200008 400 5*0 80004 500208 80004 500208 800 400 10*0
  //   80004 500208 80004 500208 800 400 10*0 80004 500208 80004 500208 800 400 10*0 80004 500208 80004
  //   500208 800 400 10*0 80004 500208 80004 500208 800 400 10*0 80004 500208 80004 500208 800 400 10*0
  //   80004 500208 80004 500208 800 400 10*0 80004 500208 80004 500208 800 400 10*0 80004 500208 80004
  //   500208 800 400 10*0 80004 500208 80004 500208 800 400 10*0 80004 500208 80004 500208 800 400 10*0
  //   80004 500208 80004 500208 800 400 10*0 80004 500208 80004 500208 800 400 10*0 80004 500208 80004
  //   500208 800 400 10*0 80004 500208 80004 500208 800 400 10*0 80004 500208 80004 500208 800 400 10*0
  //   80004 500208 80004 500208 800 400 10*0 80004 500208 80004 500208 800 400 10*0 80004 500208 80004
  //   500208 800 400 10*0 80004 500208 80004 500208 800 400 10*0 80004 500208 80004 500208 800 400 10*0
  //   80004 500208 80004 500208 800 400 10*0 80004 500208 80004 500208 800 400 10*0 80004 500208 80004
  //   500208 800 400 10*0 80004 500208 80004 500208 800 400 10*0 80004 500208 80004 500208 800 400 10*0
  //   80004 500208 80004 500208 800 400 10*0 80004 500208 80004 500208 800 400 10*0 80004 500208 80004
  //   500208 800 400 10*0 80004 500208 80004 500208 800 400 10*0 80004 500208 80004 500208 800 400 10*0
  //   80004 500208 80004 500208 800 400 10*0 80004 500208 80004 500208 800 400 10*0 80004 500208 80004
  //   500208 800 400 10*0 80004 500208 80004 500208 800 400 10*0 80004 500208 80004 500208 800 400 10*0
  //   80004 500208 80004 500208 800 400 10*0 80004 500208 80004 500208 800 400 10*0 80004 500208 80004
  //   500208 800 400 10*0 80004 500208 80004 500208 800 400 10*0 80004 500208 80004 500208 800 400 10*0
  //   80004 500208 80004 500208 800 400 10*0 80004 500208 80004 500208 800 400 10*0 80004 500208 80004
  //   500208 800 400 10*0 80004 500208 80004 500208 800 400 10*0 80004 500208 80004 500208 800 400 10*0
  //   80004 500208 80004 500208 800 400 10*0 80004 500208 80004 500208 800 400 10*0 80004 500208 80004
  //   500208 800 400 10*0 80004 500208 80004 500208 800 400 10*0 80004 500208 80004 500208 800 400 10*0
  //   80004 500208 80004 500208 800 400 10*0 80004 500208 80004 500208 800 400 10*0 80004 500208 80004
  //   500208 800 400 10*0 80004 500208 80004 500208 800 400 10*0 80004 500208 80004 500208 800 400 10*0
  //   80004 500208 80004 500208 800 80004 501008 400 8*0 80004 500208 80004 500208 800 80004 d0000a
  //   1800001 810004 4000080 400 5*0 80004 500208 80004 500208 800 80004 d0000a 1800001 810004 401000 400
  //   5*0 80004 500208 80004 500208 800 8000002 4000001 12000 400 7*0 80004 500208 80004 500208 800
  //   8000002 4020001 12000 400 7*0 80004 500208 80004 500208 800 8000002 4040001 12000 400 7*0 80004
  //   500208 80004 500208 800 8000002 4060100 400 8*0 80004 500208 80004 500208 800 80004 500018 80004
  //   500018 200008 400 5*0 80004 500208 80004 500208 800 80004 500018 80004 500018 200008 400 5*0 80004
  //   500208 80004 500208 800 400 10*0 80004 500208 80004 500208 800 400 10*0 80004 500208 80004 500208
  //   800 400 10*0 80004 500208 80004 500208 800 400 10*0 80004 500208 80004 500208 800 400 10*0 80004
  //   500208 80004 500208 800 400 10*0 80004 500208 80004 500208 800 400 10*0 80004 500208 80004 500208
  //   800 400 10*0 80004 500208 80004 500208 800 400 10*0 80004 500208 80004 500208 800 400 10*0 80004
  //   500208 80004 500208 800 400 10*0 80004 500208 80004 500208 800 400 10*0 80004 500208 80004 500208
  //   800 400 10*0 80004 500208 80004 500208 800 400 10*0 80004 500208 80004 500208 800 400 10*0 80004
  //   500208 80004 500208 800 400 10*0 80004 500208 80004 500208 800 400 10*0 80004 500208 80004 500208
  //   800 400 10*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
endmodule

module shreg (
  input  [7:0] in_1,
  input  in_2,
  output [15:0] out_3
);

  Register register_1 (.D(in_1), .Q(out_3[7:0]), .clk(in_2));  // open: en, clr
  Register register_2 (.D(out_3[7:0]), .Q(out_3[15:8]), .clk(in_2));  // open: en, clr
endmodule

module regdec (
  input  [5:0] in_1,
  input  [1:0] EA_EB,
  input  [1:0] EA_EB_2,
  output [15:0] out_4
);

  wire [1:0] demultiplexer_1_out0, demultiplexer_1_out1, demultiplexer_1_out2, demultiplexer_1_out3,
       demultiplexer_1_out4, demultiplexer_1_out5, demultiplexer_1_out6, demultiplexer_1_out7,
       demultiplexer_2_out0, demultiplexer_2_out1, demultiplexer_2_out2, demultiplexer_2_out3,
       demultiplexer_2_out4, demultiplexer_2_out5, demultiplexer_2_out6, demultiplexer_2_out7;

  assign out_4[1:0] = demultiplexer_1_out0 | demultiplexer_2_out0;  // OR_Gate or_1, 2 bits wide
  assign out_4[3:2] = demultiplexer_1_out1 | demultiplexer_2_out1;  // OR_Gate or_2, 2 bits wide
  assign out_4[5:4] = demultiplexer_1_out2 | demultiplexer_2_out2;  // OR_Gate or_3, 2 bits wide
  assign out_4[7:6] = demultiplexer_1_out3 | demultiplexer_2_out3;  // OR_Gate or_4, 2 bits wide
  assign out_4[9:8] = demultiplexer_1_out4 | demultiplexer_2_out4;  // OR_Gate or_5, 2 bits wide
  assign out_4[11:10] = demultiplexer_1_out5 | demultiplexer_2_out5;  // OR_Gate or_6, 2 bits wide
  assign out_4[13:12] = demultiplexer_1_out6 | demultiplexer_2_out6;  // OR_Gate or_7, 2 bits wide
  assign out_4[15:14] = demultiplexer_1_out7 | demultiplexer_2_out7;  // OR_Gate or_8, 2 bits wide
  Demultiplexer #(.select(3), .width(2), .disabled(0), .enable("false")) demultiplexer_1 (
    .out0(demultiplexer_1_out0), .out1(demultiplexer_1_out1), .out2(demultiplexer_1_out2),
    .out3(demultiplexer_1_out3), .out4(demultiplexer_1_out4), .out5(demultiplexer_1_out5),
    .out6(demultiplexer_1_out6), .out7(demultiplexer_1_out7), .in({EA_EB[1], EA_EB_2[1]}), .sel(in_1[5:3]));
  // Probe on in_1[5:3]
  // Probe on in_1[2:0]
  Demultiplexer #(.select(3), .width(2), .disabled(0), .enable("false")) demultiplexer_2 (
    .out0(demultiplexer_2_out0), .out1(demultiplexer_2_out1), .out2(demultiplexer_2_out2),
    .out3(demultiplexer_2_out3), .out4(demultiplexer_2_out4), .out5(demultiplexer_2_out5),
    .out6(demultiplexer_2_out6), .out7(demultiplexer_2_out7), .in({EA_EB[0], EA_EB_2[0]}), .sel(in_1[2:0]));
endmodule

module ALU (
  input  [2:0] OP,
  input  [7:0] A_8,
  input  [15:0] A,
  input  [15:0] B,
  input  _16,
  input  Carry_in,
  output [15:0] out,
  output [3:0] C_G_E_Z
);

  wire adder_1_cout, and_2_out, and_3_out, not_2_out, not_3_out, not_4_out, not_5_out, not_6_out,
       subtractor_1_bout;
  wire [7:0] undriven;
  wire [15:0] adder_1_out, and_1_out, multiplexer_1_out, not_1_out, or_1_out, subtractor_1_out, xor_1_out;

  Multiplexer #(.width(16), .disabled(0), .enable("false")) multiplexer_1 (
    .in0({undriven, A_8}), .in1(A), .out(multiplexer_1_out), .sel(_16));
  Pull_Resistor pull_resistor_1 (.node(multiplexer_1_out));
  Pull_Resistor pull_resistor_2 (.node(B));
  Adder #(.width(16)) adder_1 (.a(multiplexer_1_out), .b(B), .out(adder_1_out), .cin(Carry_in), .cout(adder_1_cout));
  assign C_G_E_Z[3] = and_2_out ? adder_1_cout : 1'bz;  // Controlled_Buffer controlled_buffer_1
  Subtractor #(.width(16)) subtractor_1 (
    .a(multiplexer_1_out), .b(B), .out(subtractor_1_out), .bin(Carry_in), .bout(subtractor_1_bout));
  assign C_G_E_Z[3] = and_3_out ? subtractor_1_bout : 1'bz;  // Controlled_Buffer controlled_buffer_2
  assign xor_1_out = multiplexer_1_out ^ B;  // XOR_Gate xor_1, 16 bits wide
  assign or_1_out = multiplexer_1_out | B;  // OR_Gate or_1, 16 bits wide
  assign and_1_out = multiplexer_1_out & B;  // AND_Gate and_1, 16 bits wide
  assign not_1_out = ~multiplexer_1_out;  // NOT_Gate not_1, 16 bits wide
  Comparator #(.width(16)) comparator_1 (.a(multiplexer_1_out), .b(B), .gt(C_G_E_Z[2]), .eq(C_G_E_Z[1]));  // open: lt
  Pull_Resistor pull_resistor_3 (.node(C_G_E_Z[3]));
  or or_2 (C_G_E_Z[0], multiplexer_1_out[0], multiplexer_1_out[1], multiplexer_1_out[2], multiplexer_1_out[3], multiplexer_1_out[4], multiplexer_1_out[5], multiplexer_1_out[6], multiplexer_1_out[7], multiplexer_1_out[8], multiplexer_1_out[9], multiplexer_1_out[10], multiplexer_1_out[11], multiplexer_1_out[12], multiplexer_1_out[13], multiplexer_1_out[14], multiplexer_1_out[15]);
  Pull_Resistor pull_resistor_4 (.node(C_G_E_Z));
  and and_2 (and_2_out, not_2_out, not_3_out, not_4_out);
  and and_3 (and_3_out, OP[0], not_5_out, not_6_out);
  not not_2 (not_2_out, OP[0]);
  not not_3 (not_3_out, OP[1]);
  not not_4 (not_4_out, OP[2]);
  not not_5 (not_5_out, OP[1]);
  not not_6 (not_6_out, OP[2]);
  Multiplexer #(.select(3), .width(16), .disabled(0), .enable("false")) multiplexer_2 (
    .in0(adder_1_out), .in1(subtractor_1_out), .in3(xor_1_out), .in4(or_1_out), .in5(and_1_out),
    .in6(not_1_out), .out(out), .sel(OP));  // open: in2, in7
endmodule

module FLG (
  input  [3:0] in_1,
  input  [3:0] cgez,
  output t_f
);

  wire [3:0] and_1_out;

  // Probe on and_1_out
  assign and_1_out = in_1 & cgez;  // AND_Gate and_1, 4 bits wide
  or or_1 (t_f, and_1_out[0], and_1_out[1], and_1_out[2], and_1_out[3]);
endmodule

module _16_2_reg (
  input  [7:0] _8_in,
  input  [15:0] _16_in,
  input  [1:0] _16_LH,
  input  [1:0] E_S,
  output [7:0] probe_GSB,
  output [7:0] probe_LSB,
  output [7:0] _8_out,
  output [15:0] _16_out
);

  wire [7:0] demultiplexer_1_out0, demultiplexer_1_out1;
  wire [15:0] demultiplexer_2_out0, multiplexer_1_out;

  Demultiplexer #(.width(8), .tristate("true"), .enable("false")) demultiplexer_1 (
    .out0(demultiplexer_1_out0), .out1(demultiplexer_1_out1), .in(_8_in), .sel(_16_LH[0]));
  Multiplexer #(.width(16), .enable("false")) multiplexer_1 (
    .in0({demultiplexer_1_out1, demultiplexer_1_out0}), .in1(_16_in), .out(multiplexer_1_out), .sel(_16_LH[1]));
  Register register_1 (.D(multiplexer_1_out[7:0]), .Q(probe_LSB), .clk(E_S[0]));  // open: en, clr
  Demultiplexer #(.width(16), .tristate("true")) demultiplexer_2 (
    .out0(demultiplexer_2_out0), .out1(_16_out), .in({probe_GSB, probe_LSB}), .sel(_16_LH[1]), .en(E_S[1]));
  Register register_2 (.D(multiplexer_1_out[15:8]), .Q(probe_GSB), .clk(E_S[0]));  // open: en, clr
  Multiplexer #(.width(8)) multiplexer_2 (
    .in0(demultiplexer_2_out0[7:0]), .in1(demultiplexer_2_out0[15:8]), .out(_8_out), .sel(_16_LH[0]),
    .en(E_S[1]));
endmodule

module _16_1_reg (
  input  [15:0] _16_in,
  input  [7:0] _8_in,
  input  [2:0] _16_S_E,
  output [15:0] _16_out,
  output [7:0] _8_out
);

  wire [15:0] multiplexer_1_out, register_1_q;
  wire [15:8] demultiplexer_1_out0;

  Multiplexer #(.width(16), .disabled(0), .enable("false")) multiplexer_1 (
    .in0({{8{1'b0}}, _8_in}), .in1(_16_in), .out(multiplexer_1_out), .sel(_16_S_E[2]));
  Demultiplexer #(.width(16), .tristate("true")) demultiplexer_1 (
    .out0({demultiplexer_1_out0, _8_out}), .out1(_16_out), .in(register_1_q), .sel(_16_S_E[2]),
    .en(_16_S_E[0]));
  Register #(.width(16)) register_1 (.D(multiplexer_1_out), .Q(register_1_q), .clk(_16_S_E[1]));  // open: en, clr
endmodule
